# Fritzing sketch meteo_sketch (saved by Fritzing 0.9.3b)
breadboards: 1

parts:
  Part1 = Arduino Uno (Rev3)
  Part2 = MicroSD Card Module
  DHT1 = DHT22 Humidity and Temperature Sensor
  DHT2 = DHT22 Humidity and Temperature Sensor

nets:
  N1: Part1.D10_PWM/SS, Part2.CS
  N2: Part1.D11_PWM/MOSI, Part2.MOSI
  N3: Part1.D12/MISO, Part2.MISO
  N4: Part1.D13/SCK, Part2.SCK
  N5: Part1.D6_PWM, DHT1.DATA
  N6: Part1.D7, DHT2.DATA
  VDD: Part1.5V, Part2.VCC, DHT1.VDD, DHT2.VDD
  GND: Part1.GND, Part2.GND, DHT1.GND, DHT2.GND

notes:
  DHT22
